// Logisim project pipeline_cpu_bubbling.circ as structural Verilog: 4 circuits, main circuit main
module main (
  output [5:0] OP
);

  wire alu_1_p4, alu_1_p9, alu_1_p10, alu_1_p14, and_1_out, bne, Branch, clk, clock_1_out, comparator_1_eq,
       comparator_2_eq, comparator_3_eq, control_1_p3, control_1_p4, control_1_p5, control_1_p6,
       control_1_p7, control_1_p8, control_1_p9, control_1_p12, control_1_p13, control_1_p14, d_ff_1_q,
       ex_mem_1_p8, ex_mem_1_p10, ex_mem_1_p11, ex_mem_1_p12, ex_mem_1_p13, Halt, hazard_unit_1_flushid,
       hazard_unit_1_flushif, hazard_unit_1_okbranch, hazard_unit_1_stallid, hazard_unit_1_stallif,
       id_ex_1_p13, id_ex_1_p15, id_ex_1_p16, id_ex_1_p17, id_ex_1_p18, id_ex_1_p19, id_ex_1_p20,
       id_ex_1_p21, mem_wb_1_p6, mem_wb_1_p8, mem_wb_1_p9, MR1_num, MR2_num, not_1_out, not_2_out, or_1_out,
       or_2_out, RegDstID, regfile_1_p1, regfile_1_p2, regfile_1_p3, regfile_1_p4, regfile_1_p13,
       regfile_1_p24, regfile_1_p25, regfile_1_p26, RegWriteEX, RegWriteMEM, statistics_1_p1,
       statistics_1_p2, statistics_1_p3, syscall_decoder_1_p5, taken, WriteBack, xor_1_out, ZeroExtendID;
  wire [3:0] syscall_decoder_1_p13_2, syscall_decoder_1_p13_3, syscall_decoder_1_p13_4,
       syscall_decoder_1_p13_5, syscall_decoder_1_p13_6;
  wire [4:0] alu_1_p13, multiplexer_6_out, R1_num, R2_num, regfile_1_p9, regfile_1_p23, regfile_1_p30;
  wire [11:0] syscall_decoder_1_p13;
  wire [15:0] statistics_1_p5;
  wire [31:0] a0, adder_1_out, adder_2_out, alu_1_p11, alu_1_p12, counter_1_q, counter_2_q, counter_3_q,
       counter_4_q, Cycle_q, hazard_unit_1_bubblenum, immediate_extender_1_p4, immediate_extender_1_p7,
       multiplexer_1_out, multiplexer_2_out, multiplexer_3_out, multiplexer_5_out, multiplexer_8_out,
       multiplexer_9_out, multiplexer_10_out, multiplexer_11_out, multiplexer_12_out, PC_q, ram_1_data,
       regfile_1_p10, regfile_1_p15, regfile_1_p16, regfile_1_p22, regfile_1_p27, regfile_1_p28,
       regfile_1_p29, register_1_q, shifter_1_out, statistics_1_p4, syscall_decoder_1_p6,
       syscall_decoder_1_p7, undriven, undriven_2, undriven_3, v0;

  Multiplexer #(.width(32), .enable("false")) multiplexer_1 (
    .in0(adder_1_out), .in1(register_1_q), .out(multiplexer_1_out), .sel(and_1_out));
  Multiplexer #(.width(32), .enable("false")) multiplexer_2 (
    .in0(multiplexer_1_out), .in1(undriven), .out(multiplexer_2_out), .sel(id_ex_1_p20));
  Counter #(.width(32), .max('hffffffff)) Cycle (.Q(Cycle_q), .clk(clk));  // open: load, D, count, carry, clr
  // Probe on Cycle_q
  Multiplexer #(.width(32), .enable("false")) multiplexer_3 (
    .in0(multiplexer_2_out), .in1(regfile_1_p27), .out(multiplexer_3_out), .sel(id_ex_1_p19));
  Counter #(.width(32), .max('hffffffff)) counter_1 (
    .count(and_1_out), .Q(counter_1_q), .clk(clk));  // open: load, D, carry, clr
  Hazard_Unit hazard_unit_1 (
    .clk(clk), .FlushIF(hazard_unit_1_flushif), .FlushID(hazard_unit_1_flushid), .IsToBranchOrJump(or_2_out),
    .WriteReg_MEM(alu_1_p13), .RT(R2_num), .RegWriteMEM(RegWriteMEM), .RS(R1_num),
    .StallIF(hazard_unit_1_stallif), .StallID(hazard_unit_1_stallid), .WriteReg_EX(regfile_1_p30),
    .RegWriteEX(RegWriteEX), .ReadRs(regfile_1_p1), .ReadRt(regfile_1_p2),
    .BubbleNum(hazard_unit_1_bubblenum), .Branch(Branch), .OkBranch(hazard_unit_1_okbranch));
  Hex_Digit_Display hex_digit_display_1 (.value(syscall_decoder_1_p13_5));  // open: dp
  Hex_Digit_Display hex_digit_display_2 (.value(syscall_decoder_1_p13_6));  // open: dp
  Counter #(.width(32), .max('hffffffff)) counter_2 (
    .count(statistics_1_p3), .Q(counter_2_q), .clk(clk));  // open: load, D, carry, clr
  // Probe on counter_2_q
  not not_1 (not_1_out, hazard_unit_1_stallif);
  // Probe on counter_1_q
  Hex_Digit_Display hex_digit_display_3 (.value(syscall_decoder_1_p13_4));  // open: dp
  Hex_Digit_Display hex_digit_display_4 (.value(syscall_decoder_1_p13_3));  // open: dp
  Counter #(.width(32), .max('hffffffff)) counter_3 (
    .count(statistics_1_p2), .Q(counter_3_q), .clk(clk));  // open: load, D, carry, clr
  // Probe on counter_3_q
  Register #(.width(32)) PC (.D(multiplexer_3_out), .en(not_1_out), .Q(PC_q), .clk(clk));  // open: clr
  Hex_Digit_Display hex_digit_display_5 (.value(syscall_decoder_1_p13_2));  // open: dp
  Hex_Digit_Display hex_digit_display_6 (.value(syscall_decoder_1_p13[11:8]));  // open: dp
  Counter #(.width(32), .max('hffffffff)) counter_4 (
    .count(statistics_1_p1), .Q(counter_4_q), .clk(clk));  // open: load, D, carry, clr
  // Probe on counter_4_q
  Adder #(.width(32)) adder_1 (.a(PC_q), .b(32'h4), .out(adder_1_out));  // open: cin, cout
  // Probe on hazard_unit_1_bubblenum
  Hex_Digit_Display hex_digit_display_7 (.value(syscall_decoder_1_p13[3:0]));  // open: dp
  Hex_Digit_Display hex_digit_display_8 (.value(syscall_decoder_1_p13[7:4]));  // open: dp
  // Statistics statistics_1: pin names not known; wires that end beside it: statistics_1_p1, statistics_1_p2, statistics_1_p3, statistics_1_p4, {OP, R1_num, R2_num, statistics_1_p5}
  ROM #(.addrWidth(10), .dataWidth(32)) rom_1 (.addr(PC_q[11:2]), .data(statistics_1_p4));  // open: sel
  Multiplexer #(.enable("false")) multiplexer_4 (.in0(clock_1_out), .in1(1'b0), .out(clk), .sel(Halt));
  Clock clock_1 (.out(clock_1_out));
  // IF_ID if_id_1: pin names not known; wires that end beside it: clk
  or or_1 (or_1_out, hazard_unit_1_flushif, and_1_out);
  not not_2 (not_2_out, hazard_unit_1_stallid);
  // Control control_1: pin names not known; wires that end beside it: OP, statistics_1_p5[5:0], control_1_p3, control_1_p4, control_1_p5, control_1_p6, control_1_p7, control_1_p8, control_1_p9, Branch, bne, control_1_p12, control_1_p13, control_1_p14
  // Immediate_Extender immediate_extender_1: pin names not known; wires that end beside it: adder_1_out, not_2_out, or_1_out, immediate_extender_1_p4, statistics_1_p5, ZeroExtendID, immediate_extender_1_p7
  Multiplexer #(.width(32), .enable("false")) multiplexer_5 (
    .in0(regfile_1_p16), .in1(regfile_1_p10), .out(multiplexer_5_out), .sel(MR2_num));
  and and_1 (and_1_out, ~clk, d_ff_1_q);  // AND_Gate
  D_Flip_Flop #(.trigger("falling")) d_ff_1 (.clk(clk), .D(taken), .Q(d_ff_1_q));  // open: Qn, preset, en, reset
  Multiplexer #(.width(5), .enable("false")) multiplexer_6 (
    .in0(R2_num), .in1(statistics_1_p5[15:11]), .out(multiplexer_6_out), .sel(RegDstID));
  Adder #(.width(32)) adder_2 (.a(shifter_1_out), .b(immediate_extender_1_p4), .out(adder_2_out));  // open: cin, cout
  // Regfile regfile_1: pin names not known; wires that end beside it: regfile_1_p1, regfile_1_p2, regfile_1_p3, regfile_1_p4, RegDstID, ZeroExtendID, R1_num, R2_num, regfile_1_p9, regfile_1_p10, v0, a0, regfile_1_p13, WriteBack, regfile_1_p15, regfile_1_p16, control_1_p14, regfile_1_p3, regfile_1_p4, regfile_1_p15, regfile_1_p16, regfile_1_p22, regfile_1_p23, regfile_1_p24, regfile_1_p25, regfile_1_p26, regfile_1_p27, regfile_1_p28, regfile_1_p29, regfile_1_p30
  Multiplexer #(.width(5), .enable("false")) multiplexer_7 (
    .in0(multiplexer_6_out), .in1({5{1'b1}}), .out(regfile_1_p23), .sel(control_1_p3));
  Multiplexer #(.width(32), .enable("false")) multiplexer_8 (
    .in0(regfile_1_p15), .in1(regfile_1_p10), .out(multiplexer_8_out), .sel(MR1_num));
  Shifter #(.width(32)) shifter_1 (.in(immediate_extender_1_p7), .\dist (5'b00010), .out(shifter_1_out));
  Register #(.width(32)) register_1 (.D(adder_2_out), .Q(register_1_q), .clk(clk));  // open: en, clr
  not not_3 (regfile_1_p13, clk);
  assign regfile_1_p22 = {{27{1'b0}}, statistics_1_p5[10:6]};  // Bit_Extender bit_extender_1
  and and_2 (taken, hazard_unit_1_okbranch, xor_1_out);
  // ID_EX id_ex_1: pin names not known; wires that end beside it: control_1_p3, control_1_p4, control_1_p5, control_1_p6, control_1_p7, control_1_p8, control_1_p9, taken, bne, control_1_p12, control_1_p13, clk, id_ex_1_p13, RegWriteEX, id_ex_1_p15, id_ex_1_p16, id_ex_1_p17, id_ex_1_p18, id_ex_1_p19, id_ex_1_p20, id_ex_1_p21
  Comparator #(.width(32)) comparator_1 (
    .a(multiplexer_8_out), .b(multiplexer_5_out), .eq(comparator_1_eq));  // open: gt, lt
  xor xor_1 (xor_1_out, bne, comparator_1_eq);
  Multiplexer #(.width(32), .enable("false")) multiplexer_9 (
    .in0(regfile_1_p27), .in1(regfile_1_p28), .out(multiplexer_9_out), .sel(regfile_1_p25));
  Multiplexer #(.width(32), .enable("false")) multiplexer_10 (
    .in0(regfile_1_p28), .in1(regfile_1_p29), .out(multiplexer_10_out), .sel(regfile_1_p25));
  Multiplexer #(.width(32), .enable("false")) multiplexer_11 (
    .in0(multiplexer_10_out), .in1(undriven_2), .out(multiplexer_11_out), .sel(regfile_1_p24));
  Comparator #(.width(5)) comparator_2 (.a(regfile_1_p9), .b(R1_num), .eq(comparator_2_eq));  // open: gt, lt
  Comparator #(.width(5)) comparator_3 (.a(regfile_1_p9), .b(R2_num), .eq(comparator_3_eq));  // open: gt, lt
  or or_2 (or_2_out, id_ex_1_p19, id_ex_1_p20, id_ex_1_p13);
  // ALU alu_1: pin names not known; wires that end beside it: multiplexer_9_out, multiplexer_11_out, id_ex_1_p21, alu_1_p4, regfile_1_p26, alu_1_p4, regfile_1_p28, regfile_1_p30, alu_1_p9, alu_1_p10, alu_1_p11, alu_1_p12, alu_1_p13, alu_1_p14
  and and_3 (MR1_num, WriteBack, comparator_2_eq);
  and and_4 (MR2_num, WriteBack, comparator_3_eq);
  // EX_MEM ex_mem_1: pin names not known; wires that end beside it: id_ex_1_p13, RegWriteEX, id_ex_1_p15, id_ex_1_p16, id_ex_1_p17, id_ex_1_p18, clk, ex_mem_1_p8, RegWriteMEM, ex_mem_1_p10, ex_mem_1_p11, ex_mem_1_p12, ex_mem_1_p13
  RAM #(.addrWidth(10), .dataWidth(32), .bus("separate")) ram_1 (
    .addr(alu_1_p11[11:2]), .din(alu_1_p12), .data(ram_1_data), .str(ex_mem_1_p12), .clk(clk),
    .ld(ex_mem_1_p13));  // open: sel, clr
  // MEM_WB mem_wb_1: pin names not known; wires that end beside it: ex_mem_1_p8, RegWriteMEM, ex_mem_1_p10, ex_mem_1_p11, clk, mem_wb_1_p6, WriteBack, mem_wb_1_p8, mem_wb_1_p9, mem_wb_1_p9
  // Syscall_Decoder syscall_decoder_1: pin names not known; wires that end beside it: alu_1_p10, alu_1_p11, ram_1_data, alu_1_p13, syscall_decoder_1_p5, syscall_decoder_1_p6, syscall_decoder_1_p7, regfile_1_p9, v0, a0, clk, syscall_decoder_1_p5, {syscall_decoder_1_p13_6, syscall_decoder_1_p13_5, syscall_decoder_1_p13_4, syscall_decoder_1_p13_3, syscall_decoder_1_p13_2, syscall_decoder_1_p13}, Halt
  Multiplexer #(.width(32), .enable("false")) multiplexer_12 (
    .in0(syscall_decoder_1_p6), .in1(syscall_decoder_1_p7), .out(multiplexer_12_out), .sel(mem_wb_1_p8));
  Multiplexer #(.width(32), .enable("false")) multiplexer_13 (
    .in0(multiplexer_12_out), .in1(undriven_3), .out(regfile_1_p10), .sel(mem_wb_1_p6));

  // Notes on the sheet:
  //   No trust 
  //   Screen
  //   contents of rom_1 (hex, n*v repeats v):
  //   20110001 8000c05 20110001 20120002 20130003 8000c09 20110001 20120002 20130003 8000c0d 20110001
  //   20120002 20130003 8000c11 20110001 20120002 20130003 c000d2e 20100001 20110001 118fc0 112020
  //   20020022 c 118882 12200001 8000c15 112020 20020022 c 20110001 118880 112020 20020022 c 12200001
  //   8000c1f 20110001 118fc0 112020 20020022 c 1188c3 112020 20020022 c 118903 112020 20020022 c 118903
  //   112020 20020022 c 118903 112020 20020022 c 118903 112020 20020022 c 118903 112020 20020022 c 118903
  //   112020 20020022 c 118903 112020 20020022 c 20100001 109fc0 139fc3 8021 2012000c 24160003 26100001
  //   3210000f 20080008 20090001 139900 2709825 132020 20020022 c 1094022 1500fff9 22100001 2018000f
  //   2188024 108700 20080008 20090001 139902 2709825 132021 20020022 c 1094022 1500fff9 108702 2c9b022
  //   12c00001 8000c50 4020 1084027 84400 3508ffff 82021 20020022 c 20110004 ae310000 8e320000 2252fffc
  //   20100000 22110001 2118020 22520004 ae500000 22310001 2118020 22520004 ae500000 22310001 2118020
  //   22520004 ae500000 22310001 2118020 22520004 ae500000 22310001 2118020 22520004 ae500000 22310001
  //   2118020 22520004 ae500000 22310001 2118020 22520004 ae500000 20090001 8c080004 1509008f ac000004
  //   20090003 8c080008 1509008b ac000008 20090006 8c08000c 15090087 ac00000c 2009000a 8c080010 15090083
  //   ac000010 2009000f 8c080014 1509007f ac000014 20090015 8c080018 1509007b ac000018 2009001c 8c08001c
  //   15090077 ac00001c 2010ffff 20110000 ae300000 22100001 22310004 ae300000 22100001 22310004 ae300000
  //   22100001 22310004 ae300000 22100001 22310004 ae300000 22100001 22310004 ae300000 22100001 22310004
  //   ae300000 22100001 22310004 ae300000 22100001 22310004 ae300000 22100001 22310004 ae300000 22100001
  //   22310004 ae300000 22100001 22310004 ae300000 22100001 22310004 ae300000 22100001 22310004 ae300000
  //   22100001 22310004 ae300000 22100001 22310004 ae300000 22100001 22310004 22100001 8020 2011003c
  //   8e130000 8e340000 274402a 11000002 ae330000 ae140000 2231fffc 1611fff8 102020 20020022 c 22100004
  //   2011003c 1611fff2 20100001 201200ff 20110001 20130003 12120005 12100004 20110001 20120002 20130003
  //   8000d26 102020 20020001 c 16310005 16320004 20110001 20120002 20130003 8000d26 132020 20020001 c
  //   2011ffff 118c00 2020 24840064 2484ff9c 14800017 2020 2484ff9c 24840064 14800013 2020 34847fff 912024
  //   1480000f 2020 34848000 912024 1480000b 24040000 8000d20 8000d26 2002000a c 20041ced 42400 3484cafe
  //   20020022 c 8000d1e 3c010000 3421baad 12020 42400 3484c0de 20020022 c 8000d1e 20100000 22100001
  //   102020 20020022 c 22100002 102020 20020022 c 22100003 102020 20020022 c 22100004 102020 20020022 c
  //   22100005 102020 20020022 c 22100006 102020 20020022 c 22100007 102020 20020022 c 22100008 102020
  //   20020022 c 3e00008
  //   PCPlus4IF
  //   Funct
  //   RS
  //   RT
  //   RD
  //   Hold Taken
  //   Branch Addr
  //   JumpAddr
  //   Immediate
  //   PCPlus4ID
  //   OkBranch
  //   JR Addr
  //   Jump Addr
  //   Branch Addr
  //   Shamt
  //   WriteReg#
  //   IsToBranchOrJump
  //   Forwarding
  //   WriteDataEX
  //   WriteReg#MEM
  //   Ignored
  //   WriteReg#WB
  //   WB_DATA
endmodule

module Hazard_Unit (
  input  clk,
  input  IsToBranchOrJump,
  input  Branch,
  input  ReadRs,
  input  ReadRt,
  input  [4:0] RT,
  input  [4:0] RS,
  input  RegWriteMEM,
  input  [4:0] WriteReg_MEM,
  input  RegWriteEX,
  input  [4:0] WriteReg_EX,
  output FlushIF,
  output FlushID,
  output StallIF,
  output StallID,
  output [31:0] BubbleNum,
  output OkBranch
);

  wire and_1_out, and_2_out, and_3_out, and_4_out, and_5_out, and_6_out, and_7_out, and_8_out,
       comparator_1_eq, comparator_2_eq, comparator_3_eq, comparator_4_eq, comparator_5_eq, comparator_6_eq,
       d_ff_1_q, d_ff_2_q, not_1_out, not_2_out, or_1_out, or_2_out, or_4_out;

  Comparator #(.width(5)) comparator_1 (.a({5{1'b0}}), .b(WriteReg_MEM), .eq(comparator_1_eq));  // open: gt, lt
  Comparator #(.width(5)) comparator_2 (.a(WriteReg_MEM), .b(RT), .eq(comparator_2_eq));  // open: gt, lt
  Comparator #(.width(5)) comparator_3 (.a(WriteReg_MEM), .b(RS), .eq(comparator_3_eq));  // open: gt, lt
  Comparator #(.width(5)) comparator_4 (.a({5{1'b0}}), .b(WriteReg_EX), .eq(comparator_4_eq));  // open: gt, lt
  Comparator #(.width(5)) comparator_5 (.a(WriteReg_EX), .b(RT), .eq(comparator_5_eq));  // open: gt, lt
  Comparator #(.width(5)) comparator_6 (.a(WriteReg_EX), .b(RS), .eq(comparator_6_eq));  // open: gt, lt
  not not_1 (not_1_out, comparator_1_eq);
  not not_2 (not_2_out, comparator_4_eq);
  and and_1 (and_1_out, comparator_2_eq, ReadRt);
  and and_2 (and_2_out, comparator_3_eq, ReadRs);
  and and_3 (and_3_out, comparator_5_eq, ReadRt);
  and and_4 (and_4_out, comparator_6_eq, ReadRs);
  or or_1 (or_1_out, and_1_out, and_2_out);
  or or_2 (or_2_out, and_3_out, and_4_out);
  and and_5 (and_5_out, not_1_out, or_1_out);
  and and_6 (and_6_out, not_2_out, or_2_out);
  D_Flip_Flop #(.trigger("falling")) d_ff_1 (
    .clk(clk), .D(IsToBranchOrJump), .Q(d_ff_1_q));  // open: Qn, preset, en, reset
  and and_7 (and_7_out, RegWriteMEM, and_5_out);
  and and_8 (and_8_out, RegWriteEX, and_6_out);
  and and_9 (FlushIF, ~clk, d_ff_1_q);  // AND_Gate
  or or_3 (StallID, and_7_out, and_8_out);
  and and_10 (OkBranch, ~StallID, Branch);  // AND_Gate
  and and_11 (FlushID, clk, d_ff_2_q);
  D_Flip_Flop #(.trigger("falling")) d_ff_2 (.clk(clk), .D(StallID), .Q(d_ff_2_q));  // open: Qn, preset, en, reset
  or or_4 (or_4_out, StallID, StallID);
  Counter #(.width(32), .max('hffffffff)) counter_1 (
    .count(or_4_out), .Q(BubbleNum), .clk(clk));  // open: load, D, carry, clr

  assign StallIF = StallID;
endmodule

module Hazard_Detector (
  input  op0,
  input  op1,
  input  op2,
  input  op3,
  input  op4,
  input  op5,
  input  Funct0,
  input  Funct1,
  input  Funct2,
  input  Funct3,
  input  Funct4,
  input  Funct5,
  output ReadRs,
  output ReadRt
);

  wire and_1_out, and_2_out, and_3_out, and_4_out, and_5_out, and_6_out, and_7_out, and_8_out, and_9_out,
       and_10_out, and_11_out, and_12_out, and_13_out, and_14_out, and_15_out, and_16_out, and_17_out,
       and_18_out, and_19_out, and_20_out, and_21_out, and_22_out, and_23_out, and_24_out, and_25_out,
       and_26_out, and_27_out, and_28_out, and_29_out, and_30_out, and_31_out, and_32_out, and_33_out,
       and_34_out, not_1_out, not_2_out, not_3_out, not_4_out, not_5_out, not_6_out, not_7_out, not_8_out,
       not_9_out, not_10_out, not_11_out, not_12_out, not_13_out, not_14_out, not_15_out, not_16_out,
       not_17_out, not_18_out, not_19_out, not_20_out, not_21_out, not_22_out, not_23_out, not_24_out,
       not_25_out, not_26_out, not_27_out, not_28_out, not_29_out, not_30_out, not_31_out, not_32_out,
       not_33_out, not_34_out, not_35_out, not_36_out, not_37_out, not_38_out, not_39_out, not_40_out,
       not_41_out, not_42_out, not_43_out, not_44_out, not_45_out, not_46_out, not_47_out, not_48_out,
       not_49_out, not_50_out, not_51_out, not_52_out, not_53_out, not_54_out, not_55_out, not_56_out,
       not_57_out, not_58_out, not_59_out, not_60_out, not_61_out, not_62_out, not_63_out, not_64_out,
       not_65_out, not_66_out, not_67_out, not_68_out, not_69_out, not_70_out, not_71_out, not_72_out,
       not_73_out, not_74_out, not_75_out, not_76_out, not_77_out, not_78_out, not_79_out, not_80_out,
       not_81_out, not_82_out, not_83_out, not_84_out, not_85_out, not_86_out, not_87_out, not_88_out,
       not_89_out, not_90_out, not_91_out, not_92_out, not_93_out, not_94_out, not_95_out, not_96_out,
       not_97_out, not_98_out, not_99_out, not_100_out, not_101_out, not_102_out, not_103_out, not_104_out,
       not_105_out, not_106_out, not_107_out, not_108_out, not_109_out, not_110_out, not_111_out,
       not_112_out, not_113_out, not_114_out, not_115_out, not_116_out, not_117_out, not_118_out,
       not_119_out, not_120_out, not_121_out, not_122_out, not_123_out, not_124_out, not_125_out,
       not_126_out, not_127_out, not_128_out, not_129_out, not_130_out, not_131_out, not_132_out,
       not_133_out, not_134_out, or_1_out, or_2_out;

  not not_1 (not_1_out, Funct1);
  not not_2 (not_2_out, Funct2);
  not not_3 (not_3_out, Funct3);
  not not_4 (not_4_out, Funct4);
  not not_5 (not_5_out, Funct5);
  not not_6 (not_6_out, Funct1);
  not not_7 (not_7_out, Funct2);
  not not_8 (not_8_out, Funct4);
  not not_9 (not_9_out, Funct5);
  not not_10 (not_10_out, Funct1);
  not not_11 (not_11_out, Funct2);
  not not_12 (not_12_out, Funct3);
  not not_13 (not_13_out, Funct4);
  not not_14 (not_14_out, Funct1);
  not not_15 (not_15_out, Funct2);
  not not_16 (not_16_out, Funct3);
  not not_17 (not_17_out, Funct5);
  not not_18 (not_18_out, Funct1);
  not not_19 (not_19_out, Funct2);
  not not_20 (not_20_out, Funct4);
  not not_21 (not_21_out, Funct1);
  not not_22 (not_22_out, Funct2);
  not not_23 (not_23_out, Funct1);
  not not_24 (not_24_out, Funct3);
  not not_25 (not_25_out, Funct5);
  not not_26 (not_26_out, Funct1);
  not not_27 (not_27_out, Funct3);
  not not_28 (not_28_out, Funct0);
  not not_29 (not_29_out, Funct1);
  not not_30 (not_30_out, Funct3);
  not not_31 (not_31_out, Funct4);
  not not_32 (not_32_out, Funct5);
  not not_33 (not_33_out, Funct1);
  not not_34 (not_34_out, Funct2);
  not not_35 (not_35_out, Funct3);
  not not_36 (not_36_out, Funct4);
  not not_37 (not_37_out, Funct5);
  not not_38 (not_38_out, Funct1);
  not not_39 (not_39_out, Funct2);
  not not_40 (not_40_out, Funct3);
  not not_41 (not_41_out, Funct4);
  not not_42 (not_42_out, Funct1);
  not not_43 (not_43_out, Funct2);
  not not_44 (not_44_out, Funct4);
  not not_45 (not_45_out, Funct5);
  not not_46 (not_46_out, Funct0);
  not not_47 (not_47_out, Funct1);
  not not_48 (not_48_out, Funct2);
  not not_49 (not_49_out, Funct3);
  not not_50 (not_50_out, Funct4);
  not not_51 (not_51_out, Funct5);
  not not_52 (not_52_out, Funct0);
  not not_53 (not_53_out, Funct1);
  not not_54 (not_54_out, Funct2);
  not not_55 (not_55_out, Funct3);
  not not_56 (not_56_out, Funct0);
  not not_57 (not_57_out, Funct1);
  not not_58 (not_58_out, Funct2);
  not not_59 (not_59_out, Funct3);
  not not_60 (not_60_out, Funct5);
  not not_61 (not_61_out, Funct1);
  not not_62 (not_62_out, Funct2);
  not not_63 (not_63_out, Funct3);
  not not_64 (not_64_out, Funct5);
  not not_65 (not_65_out, Funct1);
  not not_66 (not_66_out, Funct2);
  not not_67 (not_67_out, Funct4);
  not not_68 (not_68_out, Funct1);
  not not_69 (not_69_out, Funct2);
  not not_70 (not_70_out, Funct1);
  not not_71 (not_71_out, Funct3);
  not not_72 (not_72_out, Funct5);
  not not_73 (not_73_out, Funct1);
  not not_74 (not_74_out, Funct3);
  and and_1 (and_1_out, Funct0, not_1_out, not_2_out, not_3_out, not_4_out, not_5_out);
  and and_2 (and_2_out, Funct0, not_6_out, not_7_out, Funct3, not_8_out, not_9_out);
  and and_3 (and_3_out, Funct0, not_10_out, not_11_out, not_12_out, not_13_out, Funct5);
  and and_4 (and_4_out, Funct0, not_14_out, not_15_out, not_16_out, Funct4, not_17_out);
  and and_5 (and_5_out, Funct0, not_18_out, not_19_out, Funct3, not_20_out, Funct5);
  and and_6 (and_6_out, Funct0, not_21_out, not_22_out, Funct3, Funct4, Funct5);
  and and_7 (and_7_out, Funct0, not_23_out, Funct2, not_24_out, Funct4, not_25_out);
  and and_8 (and_8_out, Funct0, not_26_out, Funct2, not_27_out, Funct4, Funct5);
  and and_9 (and_9_out, not_28_out, not_29_out, Funct2, not_30_out, not_31_out, not_32_out);
  and and_10 (and_10_out, Funct0, not_33_out, not_34_out, not_35_out, not_36_out, not_37_out);
  and and_11 (and_11_out, Funct0, not_38_out, not_39_out, not_40_out, not_41_out, Funct5);
  and and_12 (and_12_out, Funct0, not_42_out, not_43_out, Funct3, not_44_out, not_45_out);
  and and_13 (and_13_out, not_46_out, not_47_out, not_48_out, not_49_out, not_50_out, not_51_out);
  and and_14 (and_14_out, not_52_out, not_53_out, not_54_out, not_55_out, Funct4, Funct5);
  and and_15 (and_15_out, not_56_out, not_57_out, not_58_out, not_59_out, Funct4, not_60_out);
  and and_16 (and_16_out, Funct0, not_61_out, not_62_out, not_63_out, Funct4, not_64_out);
  and and_17 (and_17_out, Funct0, not_65_out, not_66_out, Funct3, not_67_out, Funct5);
  and and_18 (and_18_out, Funct0, not_68_out, not_69_out, Funct3, Funct4, Funct5);
  and and_19 (and_19_out, Funct0, not_70_out, Funct2, not_71_out, Funct4, not_72_out);
  and and_20 (and_20_out, Funct0, not_73_out, Funct2, not_74_out, Funct4, Funct5);
  not not_75 (not_75_out, op0);
  not not_76 (not_76_out, op1);
  not not_77 (not_77_out, op2);
  not not_78 (not_78_out, op3);
  not not_79 (not_79_out, op4);
  not not_80 (not_80_out, op5);
  or or_1 (or_1_out, and_1_out, and_2_out, and_3_out, and_4_out, and_5_out, and_6_out, and_7_out, and_8_out, and_9_out);
  not not_81 (not_81_out, op0);
  not not_82 (not_82_out, op1);
  not not_83 (not_83_out, op3);
  not not_84 (not_84_out, op4);
  not not_85 (not_85_out, op5);
  not not_86 (not_86_out, op0);
  not not_87 (not_87_out, op1);
  not not_88 (not_88_out, op3);
  not not_89 (not_89_out, op4);
  not not_90 (not_90_out, op0);
  not not_91 (not_91_out, op1);
  not not_92 (not_92_out, op4);
  not not_93 (not_93_out, op5);
  not not_94 (not_94_out, op0);
  not not_95 (not_95_out, op1);
  not not_96 (not_96_out, op4);
  not not_97 (not_97_out, op1);
  not not_98 (not_98_out, op2);
  not not_99 (not_99_out, op3);
  not not_100 (not_100_out, op1);
  not not_101 (not_101_out, op3);
  not not_102 (not_102_out, op0);
  not not_103 (not_103_out, op1);
  not not_104 (not_104_out, op2);
  not not_105 (not_105_out, op4);
  not not_106 (not_106_out, op5);
  not not_107 (not_107_out, op0);
  not not_108 (not_108_out, op1);
  not not_109 (not_109_out, op2);
  not not_110 (not_110_out, op4);
  not not_111 (not_111_out, op0);
  not not_112 (not_112_out, op1);
  not not_113 (not_113_out, op3);
  not not_114 (not_114_out, op5);
  not not_115 (not_115_out, op0);
  not not_116 (not_116_out, op1);
  not not_117 (not_117_out, op2);
  not not_118 (not_118_out, op3);
  not not_119 (not_119_out, op4);
  not not_120 (not_120_out, op5);
  or or_2 (or_2_out, and_10_out, and_11_out, and_12_out, and_13_out, and_14_out, and_15_out, and_16_out, and_17_out, and_18_out, and_19_out, and_20_out);
  not not_121 (not_121_out, op0);
  not not_122 (not_122_out, op1);
  not not_123 (not_123_out, op2);
  not not_124 (not_124_out, op4);
  not not_125 (not_125_out, op5);
  not not_126 (not_126_out, op0);
  not not_127 (not_127_out, op1);
  not not_128 (not_128_out, op2);
  not not_129 (not_129_out, op4);
  not not_130 (not_130_out, op0);
  not not_131 (not_131_out, op2);
  not not_132 (not_132_out, op3);
  not not_133 (not_133_out, op4);
  not not_134 (not_134_out, op5);
  and and_21 (and_21_out, not_75_out, not_76_out, not_77_out, not_78_out, not_79_out, not_80_out, or_1_out);
  and and_22 (and_22_out, not_81_out, not_82_out, op2, not_83_out, not_84_out, not_85_out);
  and and_23 (and_23_out, not_86_out, not_87_out, op2, not_88_out, not_89_out, op5);
  and and_24 (and_24_out, not_90_out, not_91_out, op2, op3, not_92_out, not_93_out);
  and and_25 (and_25_out, not_94_out, not_95_out, op2, op3, not_96_out, op5);
  and and_26 (and_26_out, op0, not_97_out, not_98_out, not_99_out, op4, op5);
  and and_27 (and_27_out, op0, not_100_out, op2, not_101_out, op4, op5);
  and and_28 (and_28_out, not_102_out, not_103_out, not_104_out, op3, not_105_out, not_106_out);
  and and_29 (and_29_out, not_107_out, not_108_out, not_109_out, op3, not_110_out, op5);
  and and_30 (and_30_out, not_111_out, not_112_out, op2, not_113_out, op4, not_114_out);
  and and_31 (and_31_out, not_115_out, not_116_out, not_117_out, not_118_out, not_119_out, not_120_out, or_2_out);
  and and_32 (and_32_out, not_121_out, not_122_out, not_123_out, op3, not_124_out, not_125_out);
  and and_33 (and_33_out, not_126_out, not_127_out, not_128_out, op3, not_129_out, op5);
  and and_34 (and_34_out, not_130_out, op1, not_131_out, not_132_out, not_133_out, not_134_out);
  or or_3 (ReadRs, and_21_out, and_22_out, and_23_out, and_24_out, and_25_out, and_26_out, and_27_out, and_28_out, and_29_out, and_30_out);
  or or_4 (ReadRt, and_31_out, and_32_out, and_33_out, and_34_out);
endmodule

module testes (
  input  clk,
  input  in_2
);

  wire d_ff_1_q, not_1_out;

  not not_1 (not_1_out, clk);
  D_Flip_Flop #(.trigger("falling")) d_ff_1 (.clk(not_1_out), .D(in_2), .Q(d_ff_1_q));  // open: Qn, preset, en, reset
endmodule
